# Fritzing sketch gloves_soldered (saved by Fritzing 0.9.4)

parts:
  Part1 = Arduino Nano 33 BLE Sense
  LED2 = RGB LED (com. anode, rbg) [package="5 mm [THT]"]
  LED1 = RGB LED (com. anode, rbg) [package="5 mm [THT]"]
  LED3 = RGB LED (com. anode, rbg) [package="5 mm [THT]"]
  S1 = Toggle Switch [package=THT]
  R1 = Basic Flex Resistor
  R2 = Basic Flex Resistor
  R3 = Basic Flex Resistor
  R4 = Basic Flex Resistor
  R5 = Basic Flex Resistor
  VCC1 = Battery
  R11 = Resistor [tolerance=±5% resistance=47k package="1206 [SMD]"]  # not connected
  R12 = Resistor [tolerance=±5% resistance=47k package="1206 [SMD]"]  # not connected
  R13 = Resistor [tolerance=±5% resistance=47k package="1206 [SMD]"]  # not connected
  R14 = Resistor [tolerance=±5% resistance=47k package="1206 [SMD]"]  # not connected
  R15 = Resistor [tolerance=±5% resistance=47k package="1206 [SMD]"]  # not connected
  R16 = Resistor [tolerance=±5% resistance=1k package="1206 [SMD]"]  # not connected

nets:
  N1: Part1.GND, Part1.A7, LED1.common_anode, LED3.common_anode, VCC1.-
  N2: Part1.D2, S1.L1
  N3: Part1.D4, LED3.red_cathode
  N4: Part1.D5~, LED3.green_cathode
  N5: Part1.D6~, LED3.blue_cathode
  N6: Part1.D7, LED2.red_cathode
  N7: Part1.D8, LED2.green_cathode
  N8: Part1.D9~, LED2.blue_cathode
  N9: Part1.D10~, LED1.red_cathode
  N10: Part1.D11/MOSI, Part1.+5V, LED1.green_cathode
  N11: Part1.D12~/MISO, LED1.blue_cathode
  N12: Part1.VIN, VCC1.+
  N13: Part1.A5, R5.pin_1
  N14: Part1.A4, R4.pin_1
  N15: Part1.A3, R3.pin_1
  N16: Part1.A2, R2.pin_1
  N17: Part1.A1, R1.pin_1
  N18: Part1.3V3, S1.COM, R1.Pin_2, R2.Pin_2, R3.Pin_2, R4.Pin_2, R5.Pin_2

notes:
  18650 Battery shield V3

custom parts:
  Arduino Nano 33 BLE Sense: The Nano 33 BLE Sense (without headers) is Arduino’s 3.3V AI enabled board in the smallest available form factor: 45x18mm! The Arduino Nano 33 BLE Sense is a completely new board on a well-known form factor. It comes with a series of embedded sensors: 9 axis inertial sensor: what makes this board ideal for wearable devices humidity, and temperature sensor: to get highly accurate measurements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
  Battery: Your standard 2x 18650 battery pack (7,4 Volts)
